// Logisim project cache_simulation.circ as structural Verilog: 4 circuits, main circuit main
module main (
);

  wire cache_1_cachedone, cache_1_memenable, cache_1_memweout, clk_out, cpu_1_we, memory_1_done;
  wire [31:0] cache_1_memaddrout, cache_1_memdataout, cache_1_readdataout, cpu_1_address, cpu_1_data,
       memory_1_dataout;

  Clock clk (.out(clk_out));
  cpu cpu_1 (
    .clk(clk_out), .cacheData(cache_1_readdataout), .cacheDone(cache_1_cachedone), .address(cpu_1_address),
    .data(cpu_1_data), .we(cpu_1_we));
  cache cache_1 (
    .clk(clk_out), .requestAddr(cpu_1_address), .requestData(cpu_1_data), .requestWe(cpu_1_we),
    .memDataIn(memory_1_dataout), .memDone(memory_1_done), .readDataOut(cache_1_readdataout),
    .cacheDone(cache_1_cachedone), .memAddrOut(cache_1_memaddrout), .memDataOut(cache_1_memdataout),
    .memWeOut(cache_1_memweout), .memEnable(cache_1_memenable));
  memory memory_1 (
    .clk(clk_out), .address(cache_1_memaddrout), .data(cache_1_memdataout), .we(cache_1_memweout),
    .memoryEnable(cache_1_memenable), .dataOut(memory_1_dataout), .done(memory_1_done));
endmodule

module cpu (
  input  clk,
  input  [31:0] cacheData,
  input  cacheDone,
  output [31:0] address,
  output [31:0] data,
  output we
);
endmodule

module cache (
  input  clk,
  input  [31:0] requestAddr,
  input  [31:0] requestData,
  input  requestWe,
  input  [31:0] memDataIn,
  input  memDone,
  output [31:0] readDataOut,
  output cacheDone,
  output [31:0] memAddrOut,
  output [31:0] memDataOut,
  output memWeOut,
  output memEnable
);
endmodule

module memory (
  input  clk,
  input  [31:0] address,
  input  [31:0] data,
  input  we,
  input  memoryEnable,
  output [31:0] dataOut,
  output done
);
endmodule
